# Fritzing sketch plate (saved by Fritzing 0.9.4)
breadboards: 1

parts:
  Компонент1 = Arduino Mega 2560 (Rev3)
  Компонент2 = Arduino Ethernet Shield (Rev3)  # not connected
  LED2 = smd LED [color="Red (633nm)" package="0805 [SMD]"]
  LED3 = smd LED [color="Red (633nm)" package="0805 [SMD]"]
  S1 = Pushbutton [package="[SMD]"]
  R1 = Resistor [tolerance=±5% resistance=220 package=THT]  # not connected
  R2 = Resistor [tolerance=±5% resistance=220 package=THT]  # not connected
  R3 = Resistor [tolerance=±5% resistance=220 package=THT]
  LED4 = smd LED [color="Red (633nm)" package="0805 [SMD]"]
  R4 = Resistor [tolerance=±5% resistance=1k package="1206 [SMD]"]

nets:
  N1: Компонент1.D17_PWM/RX2, LED3.anode
  N2: Компонент1.D16_PWM/TX2, LED2.anode
  N3: Компонент1.D15/RX3, LED4.anode
  N4: Компонент1.D14/TX3, S1.Pin_1, S1.Pin_2, R4.Pin_1
  N5: Компонент1.5V, S1.Pin_4
  N6: Компонент1.GND, R3.Pin_0, R4.Pin_0
